# Fritzing sketch Circuits (saved by Fritzing 0.9.3b)
circuit board: 8.46667cm x 5.64444cm
breadboards: 1

parts:
  U1 = ESP32S-HiLetgo [part_number=ESP32S-HiLetgo]
  DHT1 = DHT11 Humitidy and Temperature Sensor
  Part1 = SRF05 Ultrasonic Rangefinder
  PART1 = SparkFun Soil Moisture Sensor [part_number=SEN-13322]
  Display1 = LCD screen 16x2 IIC [part_number=101290]
  KY-1 = Keyes Relay [package=THT]
  J1 = Buzzer
  BAT1 = BC9VPC [package=bc9vpc]
  WATER_PUMP1 = water pump/motor  # not connected

nets (from the breadboard view):
  N1: U1.GPIO39, PART1.SIG
  N2: U1.GPIO35, KY-1.ground
  N3: U1.GPIO9, Part1.Trig
  N4: U1.GPIO10, Part1.Echo
  GND: U1.GPIO11, DHT1.GND, Part1.GND, PART1.GND, KY-1.power, KY-1.C, J1.pin1, BAT1.V-
  VCC: U1.VIN, DHT1.VDD, Part1.VCC, PART1.VCC, KY-1.signal, KY-1.NO, BAT1.V+
  N5: U1.GPIO2, DHT1.DATA
  N6: U1.GPIO3, Display1.SDA
  N7: U1.GPIO23, Display1.SCL

notes:
  Red cable - +ve
  Black cable - -ve

custom parts:
  ESP32S-HiLetgo: HiLetgo ESP-WROOM-32 ESP32 ESP-32S Development Board 2.4GHz Dual-Mode WiFi + Bluetooth Dual Cores Microcontroller The ESP32 integrated with Antenna switches, RF Balun, power amplifiers, low-noise amplifiers, filters, and management modules, and the entire solution occupies the least area of PCB. 2.4 GHz Wi-Fi plus Bluetooth dual-mode chip, with TSMC Ultra-low power consumption 40nm technology,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
  DHT11 Humitidy and Temperature Sensor: DHT11 Humidity and Temperature Sensor
  SparkFun Soil Moisture Sensor: The SparkFun Soil Moisture Sensor is a simple breakout for measuring the moisture in soil and similar materials.
  LCD screen 16x2 IIC: LCD screen with HD44780 controller enables showing text, symbols, value or anything else that comes from Croduino/Arduino. It is capable of showing 16 symbols in two lines and therefore can be used in many projects that need to send clearly visible and legible output information.. • Color of symbols: White • Backlight: Blue • Dimensions: 80 x 36 x 12 mm • Screen dimensions: 64.5 x 16 mm •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
  Keyes Relay: The Keyes 5V relay module is suitable for SCM development, home appliance control. It uses a 5V~12V TIL control signal which can control DC / AC signal.
  Buzzer: Fixed frequency buzzer
  water pump/motor: WATER PUMP BY ARDUBLOCKTR
