# Fritzing sketch Circuits1 (saved by Fritzing 0.9.3b)
circuit board: 8.46667cm x 5.64444cm
breadboards: 1

parts:
  part = ESP32S-HiLetgo [part_number=ESP32S-HiLetgo]
  DHT11 = DHT11 Humitidy and Temperature Sensor
  Ultrasonic_sensor = SRF05 Ultrasonic Rangefinder
  Soil_Moisture_Sensor = SparkFun Soil Moisture Sensor [part_number=SEN-13322]
  LCD_Display_(I2C) = LCD screen 16x2 IIC [part_number=101290]
  5V_Relay_Module = Keyes Relay [package=THT]
  Buzzer = Buzzer
  Battery_9V = BC9VPC [package=bc9vpc]
  Water_Pump = water pump/motor  # not connected

nets:
  N1: part.GPIO39, Soil_Moisture_Sensor.SIG
  N2: part.GPIO35, 5V_Relay_Module.ground
  N3: part.GPIO9, Ultrasonic_sensor.Trig
  N4: part.GPIO10, Ultrasonic_sensor.Echo
  GND: part.GPIO11, DHT11.GND, Ultrasonic_sensor.GND, Soil_Moisture_Sensor.GND, 5V_Relay_Module.power, Buzzer.pin1, Battery_9V.V-
  VCC: part.VIN, DHT11.VDD, Ultrasonic_sensor.VCC, Soil_Moisture_Sensor.VCC, 5V_Relay_Module.signal, 5V_Relay_Module.NC, 5V_Relay_Module.C, 5V_Relay_Module.NO, Battery_9V.V+
  N5: part.GPIO2, DHT11.DATA
  N6: part.GPIO3, LCD_Display_(I2C).SDA
  N7: part.GPIO23, LCD_Display_(I2C).SCL

custom parts:
  ESP32S-HiLetgo: HiLetgo ESP-WROOM-32 ESP32 ESP-32S Development Board 2.4GHz Dual-Mode WiFi + Bluetooth Dual Cores Microcontroller The ESP32 integrated with Antenna switches, RF Balun, power amplifiers, low-noise amplifiers, filters, and management modules, and the entire solution occupies the least area of PCB. 2.4 GHz Wi-Fi plus Bluetooth dual-mode chip, with TSMC Ultra-low power consumption 40nm technology,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
  DHT11 Humitidy and Temperature Sensor: DHT11 Humidity and Temperature Sensor
  SparkFun Soil Moisture Sensor: The SparkFun Soil Moisture Sensor is a simple breakout for measuring the moisture in soil and similar materials.
  LCD screen 16x2 IIC: LCD screen with HD44780 controller enables showing text, symbols, value or anything else that comes from Croduino/Arduino. It is capable of showing 16 symbols in two lines and therefore can be used in many projects that need to send clearly visible and legible output information.. • Color of symbols: White • Backlight: Green • Dimensions: 80 x 36 x 12 mm • Screen dimensions: 64.5 x 16 mm •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
  Keyes Relay: The Keyes 5V relay module is suitable for SCM development, home appliance control. It uses a 5V~12V TIL control signal which can control DC / AC signal.
  Buzzer: Fixed frequency buzzer
  water pump/motor: WATER PUMP BY ARDUBLOCKTR
